// Logisim project BasicComputer.circ as structural Verilog: 1 circuit, main circuit CompleteComputer
module CompleteComputer (
  input  [3:0] in_1
);

  wire control_unit_1_acclr, control_unit_1_ace, control_unit_1_acinr, control_unit_1_acld,
       control_unit_1_alucin, control_unit_1_arclr, control_unit_1_are, control_unit_1_arinr,
       control_unit_1_arld, control_unit_1_drclr, control_unit_1_dre, control_unit_1_drinc,
       control_unit_1_drld, control_unit_1_irclr, control_unit_1_ire, control_unit_1_irld,
       control_unit_1_pcclr, control_unit_1_pce, control_unit_1_pcinr, control_unit_1_pcld,
       control_unit_1_read, control_unit_1_scclr, control_unit_1_trclr, control_unit_1_trinr,
       control_unit_1_trld, control_unit_1_write, CP_out, Reset_out;
  wire [3:0] AC_a, AC_a_2, AC_a_3, AC_a_4, controlled_buffer_1_out, controlled_buffer_1_out_2,
       controlled_buffer_1_out_3, controlled_buffer_3_out, DR_a, DR_a_2, DR_a_3, DR_a_4, IR_a, IR_a_2,
       IR_a_3, IR_a_4;
  wire [7:0] INPR_a, OUTR_a;
  wire [11:0] AR_a, PC_a;
  wire [15:0] bit16_alsu_1_f, ram_1_dout, TR_a;

  Clock CP (.out(CP_out));
  Button Reset (.out(Reset_out));
  Control_Unit control_unit_1 (
    .IR({IR_a_4, IR_a_3, IR_a_2, IR_a}), .R(1'b0), .IEN(1'b1), .FGI(CP_out), .FGO(Reset_out),
    .ALUCin(control_unit_1_alucin), .SCCLR(control_unit_1_scclr), .ACLD(control_unit_1_acld),
    .ACINR(control_unit_1_acinr), .ACCLR(control_unit_1_acclr), .ARLD(control_unit_1_arld),
    .ARINR(control_unit_1_arinr), .ARCLR(control_unit_1_arclr), .DRLD(control_unit_1_drld),
    .DRINC(control_unit_1_drinc), .DRCLR(control_unit_1_drclr), .IRLD(control_unit_1_irld),
    .IRCLR(control_unit_1_irclr), .READ(control_unit_1_read), .WRITE(control_unit_1_write),
    .PCLD(control_unit_1_pcld), .PCINR(control_unit_1_pcinr), .PCCLR(control_unit_1_pcclr),
    .TRLD(control_unit_1_trld), .TRINR(control_unit_1_trinr), .TRCLR(control_unit_1_trclr),
    .ARE(control_unit_1_are), .PCE(control_unit_1_pce), .DRE(control_unit_1_dre), .ACE(control_unit_1_ace),
    .IRE(control_unit_1_ire));  // open: SC, CLR, ALUS, TRE, MEME, ELD, ECLR, ECMP, IENSET, IENCLR, SCLR, RSET, RCLR, FGICLR, FGOCLR, CPE
  Bit16_ALSU bit16_alsu_1 (
    .A({AC_a_4, AC_a_3, AC_a_2, AC_a}), .B({DR_a_4, DR_a_3, DR_a_2, DR_a}), .S(in_1), .F(bit16_alsu_1_f));  // open: C_prev, C_next
  RAM #(.addrWidth(12), .dataWidth(16)) ram_1 (
    .addr(AR_a), .we(control_unit_1_irclr), .oe(control_unit_1_irld), .clk(CP_out),
    .din({controlled_buffer_3_out, controlled_buffer_1_out_3, controlled_buffer_1_out_2, controlled_buffer_1_out}),
    .dout(ram_1_dout));
  Bit12_Register AR (
    .I({controlled_buffer_1_out_3, controlled_buffer_1_out_2, controlled_buffer_1_out}),
    .Load(control_unit_1_acinr), .INR(control_unit_1_acclr), .CLR(control_unit_1_arld), .CP(CP_out), .A(AR_a));  // open: C
  Bit12_Register PC (
    .I({controlled_buffer_1_out_3, controlled_buffer_1_out_2, controlled_buffer_1_out}),
    .Load(control_unit_1_read), .INR(control_unit_1_write), .CLR(control_unit_1_pcld), .CP(CP_out), .A(PC_a));  // open: C
  Bit16_Register DR (
    .I({controlled_buffer_3_out, controlled_buffer_1_out_3, controlled_buffer_1_out_2, controlled_buffer_1_out}),
    .Load(control_unit_1_arinr), .INR(control_unit_1_arclr), .CLR(control_unit_1_drld), .CP(CP_out),
    .A({DR_a_4, DR_a_3, DR_a_2, DR_a}));  // open: C
  Bit16_Register AC (
    .I(bit16_alsu_1_f), .Load(control_unit_1_alucin), .INR(control_unit_1_scclr), .CLR(control_unit_1_acld),
    .CP(CP_out), .A({AC_a_4, AC_a_3, AC_a_2, AC_a}));  // open: C
  Bit8_Register INPR (.CLR(Reset_out), .CP(CP_out), .A(INPR_a));  // open: I, Load, INR, C
  Bit16_Register IR (
    .I({controlled_buffer_3_out, controlled_buffer_1_out_3, controlled_buffer_1_out_2, controlled_buffer_1_out}),
    .Load(control_unit_1_drinc), .INR(1'b0), .CLR(control_unit_1_drclr), .CP(CP_out),
    .A({IR_a_4, IR_a_3, IR_a_2, IR_a}));  // open: C
  Bit16_Register TR (
    .I({controlled_buffer_3_out, controlled_buffer_1_out_3, controlled_buffer_1_out_2, controlled_buffer_1_out}),
    .Load(control_unit_1_pcinr), .INR(control_unit_1_pcclr), .CLR(control_unit_1_trld), .CP(CP_out), .A(TR_a));  // open: C
  Bit8_Register OUTR (.CLR(Reset_out), .CP(CP_out), .A(OUTR_a));  // open: I, Load, INR, C
  Hex_Digit_Display hex_digit_display_1 (.value(ram_1_dout[15:12]));  // open: dp
  Hex_Digit_Display hex_digit_display_2 (.value(ram_1_dout[11:8]));  // open: dp
  Hex_Digit_Display hex_digit_display_3 (.value(AR_a[11:8]));  // open: dp
  Hex_Digit_Display hex_digit_display_4 (.value(AR_a[7:4]));  // open: dp
  Hex_Digit_Display hex_digit_display_5 (.value(PC_a[11:8]));  // open: dp
  Hex_Digit_Display hex_digit_display_6 (.value(PC_a[7:4]));  // open: dp
  Hex_Digit_Display hex_digit_display_7 (.value(DR_a_4));  // open: dp
  Hex_Digit_Display hex_digit_display_8 (.value(DR_a_3));  // open: dp
  Hex_Digit_Display hex_digit_display_9 (.value(AC_a_4));  // open: dp
  Hex_Digit_Display hex_digit_display_10 (.value(AC_a_3));  // open: dp
  Hex_Digit_Display hex_digit_display_11 (.value(INPR_a[7:4]));  // open: dp
  Hex_Digit_Display hex_digit_display_12 (.value(INPR_a[3:0]));  // open: dp
  Hex_Digit_Display hex_digit_display_13 (.value(IR_a_4));  // open: dp
  Hex_Digit_Display hex_digit_display_14 (.value(IR_a_3));  // open: dp
  Hex_Digit_Display hex_digit_display_15 (.value(TR_a[15:12]));  // open: dp
  Hex_Digit_Display hex_digit_display_16 (.value(TR_a[11:8]));  // open: dp
  Hex_Digit_Display hex_digit_display_17 (.value(OUTR_a[7:4]));  // open: dp
  Hex_Digit_Display hex_digit_display_18 (.value(OUTR_a[3:0]));  // open: dp
  Hex_Digit_Display hex_digit_display_19 (.value(ram_1_dout[7:4]));  // open: dp
  Hex_Digit_Display hex_digit_display_20 (.value(ram_1_dout[3:0]));  // open: dp
  Hex_Digit_Display hex_digit_display_21 (.value(AR_a[3:0]));  // open: dp
  Hex_Digit_Display hex_digit_display_22 (.value(PC_a[3:0]));  // open: dp
  Hex_Digit_Display hex_digit_display_23 (.value(DR_a_2));  // open: dp
  Hex_Digit_Display hex_digit_display_24 (.value(DR_a));  // open: dp
  Hex_Digit_Display hex_digit_display_25 (.value(AC_a_2));  // open: dp
  Hex_Digit_Display hex_digit_display_26 (.value(AC_a));  // open: dp
  Hex_Digit_Display hex_digit_display_27 (.value(IR_a_2));  // open: dp
  Hex_Digit_Display hex_digit_display_28 (.value(IR_a));  // open: dp
  Hex_Digit_Display hex_digit_display_29 (.value(TR_a[7:4]));  // open: dp
  Hex_Digit_Display hex_digit_display_30 (.value(TR_a[3:0]));  // open: dp
  assign {controlled_buffer_1_out_3, controlled_buffer_1_out_2, controlled_buffer_1_out} = control_unit_1_trinr ? AR_a : 12'bz;  // Controlled_Buffer controlled_buffer_1
  assign {controlled_buffer_1_out_3, controlled_buffer_1_out_2, controlled_buffer_1_out} = control_unit_1_trclr ? PC_a : 12'bz;  // Controlled_Buffer controlled_buffer_2
  assign {controlled_buffer_3_out, controlled_buffer_1_out_3, controlled_buffer_1_out_2, controlled_buffer_1_out} = control_unit_1_are ? {DR_a_4, DR_a_3, DR_a_2, DR_a} : 16'bz;  // Controlled_Buffer controlled_buffer_3
  Hex_Digit_Display hex_digit_display_31 (.value(controlled_buffer_3_out));  // open: dp
  assign {controlled_buffer_3_out, controlled_buffer_1_out_3, controlled_buffer_1_out_2, controlled_buffer_1_out} = control_unit_1_pce ? {AC_a_4, AC_a_3, AC_a_2, AC_a} : 16'bz;  // Controlled_Buffer controlled_buffer_4
  Hex_Digit_Display hex_digit_display_32 (.value(controlled_buffer_1_out_3));  // open: dp
  Hex_Digit_Display hex_digit_display_33 (.value(controlled_buffer_1_out_2));  // open: dp
  assign {controlled_buffer_3_out, controlled_buffer_1_out_3, controlled_buffer_1_out_2, controlled_buffer_1_out} = control_unit_1_dre ? {IR_a_4, IR_a_3, IR_a_2, IR_a} : 16'bz;  // Controlled_Buffer controlled_buffer_5
  assign {controlled_buffer_3_out, controlled_buffer_1_out_3, controlled_buffer_1_out_2, controlled_buffer_1_out} = control_unit_1_ire ? ram_1_dout : 16'bz;  // Controlled_Buffer controlled_buffer_6
  Hex_Digit_Display hex_digit_display_34 (.value(controlled_buffer_1_out));  // open: dp
  assign {controlled_buffer_3_out, controlled_buffer_1_out_3, controlled_buffer_1_out_2, controlled_buffer_1_out} = control_unit_1_ace ? TR_a : 16'bz;  // Controlled_Buffer controlled_buffer_7
endmodule
